# Fritzing sketch arduino-diagram (saved by Fritzing 0.9.3b)
breadboards: 1

parts:
  Part1 = Arduino Uno (Rev3) - ICSP
  Mod1 = KY-019 5V Relay Module [package="Breakout board"]
  S1 = Pushbutton [package="[THT]"]
  S2 = Pushbutton [package="[THT]"]
  J1 = Basic Servo
  Mod2 = KY-019 5V Relay Module [package="Breakout board"]

nets:
  N1: Part1.D8, Mod1.Common
  N2: Part1.D9_PWM, Mod2.Common
  N3: Part1.D7, J1.pulse
  GND: Part1.GND, Mod1.-, Mod1.NC, J1.gnd, Mod2.-
  VIN: Part1.VIN, Mod1.+, Mod1.NO, S1.Pin_1, S1.Pin_2, S2.Pin_3, S2.Pin_4, J1.vcc, Mod2.+, Mod2.NC, Mod2.NO
  N4: Mod1.S, S1.Pin_3, S1.Pin_4
  N5: S2.Pin_1, S2.Pin_2, Mod2.S

custom parts:
  KY-019 5V Relay Module: KY-019 5V Relay module, used to control AC circuits. (Special thanks to vanepp for fixing the PCB holes and other errors)
